// Logisim project 4bit_sort.circ as structural Verilog
module _1bit_swap (
  input  I1,
  input  I2,
  input  S,
  output O1,
  output O2
);

  wire and_1_out, and_2_out, or_1_out, or_2_out, xor_1_out, xor_2_out;

  xor xor_1 (xor_1_out, S, or_1_out);
  and and_1 (and_1_out, I1, S);
  or or_1 (or_1_out, S, I1);
  or or_2 (or_2_out, S, I2);
  and and_2 (and_2_out, S, I2);
  xor xor_2 (xor_2_out, or_2_out, S);
  or or_3 (O1, xor_1_out, and_2_out);
  or or_4 (O2, and_1_out, xor_2_out);
endmodule

module _4bit_swap (
  input  [3:0] in_1,
  input  [3:0] in_2,
  input  in_3,
  output [3:0] out_4,
  output [3:0] out_5
);

  _1bit_swap u_1bit_swap_1 (.I1(in_1[0]), .I2(in_2[0]), .S(in_3), .O1(out_4[0]), .O2(out_5[0]));
  _1bit_swap u_1bit_swap_2 (.I1(in_1[1]), .I2(in_2[1]), .S(in_3), .O1(out_4[1]), .O2(out_5[1]));
  _1bit_swap u_1bit_swap_3 (.I1(in_1[2]), .I2(in_2[2]), .S(in_3), .O1(out_4[2]), .O2(out_5[2]));
  _1bit_swap u_1bit_swap_4 (.I1(in_1[3]), .I2(in_2[3]), .S(in_3), .O1(out_4[3]), .O2(out_5[3]));
endmodule

module _4bit_sort (
  input  [3:0] in_1,
  input  [3:0] in_2,
  input  [3:0] in_3,
  input  [3:0] in_4,
  output [3:0] out_5,
  output [3:0] out_6,
  output [3:0] out_7,
  output [3:0] out_8
);

  wire comparator_1_gt, comparator_2_gt, comparator_3_gt, comparator_4_gt, comparator_5_gt;
  wire [3:0] n4bit_swap_1_out_4, n4bit_swap_1_out_5, n4bit_swap_2_out_4, n4bit_swap_2_out_5,
       n4bit_swap_3_out_4, n4bit_swap_4_out_5;

  Comparator #(.width(4), .mode("unsigned")) comparator_1 (.a(in_1), .b(in_2), .gt(comparator_1_gt));  // open: eq, lt
  Comparator #(.width(4), .mode("unsigned")) comparator_2 (.a(in_3), .b(in_4), .gt(comparator_2_gt));  // open: eq, lt
  _4bit_swap u_4bit_swap_1 (
    .in_1(in_1), .in_2(in_2), .in_3(comparator_1_gt), .out_4(n4bit_swap_1_out_4), .out_5(n4bit_swap_1_out_5));
  _4bit_swap u_4bit_swap_2 (
    .in_1(in_3), .in_2(in_4), .in_3(comparator_2_gt), .out_4(n4bit_swap_2_out_4), .out_5(n4bit_swap_2_out_5));
  Comparator #(.width(4), .mode("unsigned")) comparator_3 (
    .a(n4bit_swap_1_out_5), .b(n4bit_swap_2_out_5), .gt(comparator_3_gt));  // open: eq, lt
  Comparator #(.width(4), .mode("unsigned")) comparator_4 (
    .a(n4bit_swap_1_out_4), .b(n4bit_swap_2_out_4), .gt(comparator_4_gt));  // open: eq, lt
  _4bit_swap u_4bit_swap_3 (
    .in_1(n4bit_swap_1_out_5), .in_2(n4bit_swap_2_out_5), .in_3(comparator_3_gt), .out_4(n4bit_swap_3_out_4),
    .out_5(out_8));
  _4bit_swap u_4bit_swap_4 (
    .in_1(n4bit_swap_1_out_4), .in_2(n4bit_swap_2_out_4), .in_3(comparator_4_gt), .out_4(out_5),
    .out_5(n4bit_swap_4_out_5));
  Comparator #(.width(4), .mode("unsigned")) comparator_5 (
    .a(n4bit_swap_3_out_4), .b(n4bit_swap_4_out_5), .gt(comparator_5_gt));  // open: eq, lt
  _4bit_swap u_4bit_swap_5 (
    .in_1(n4bit_swap_3_out_4), .in_2(n4bit_swap_4_out_5), .in_3(comparator_5_gt), .out_4(out_6), .out_5(out_7));

  // Other names for the same wires on the sheet: yj[3:0] = out_6
endmodule
