// Logisim project CHALLENGE!!!.circ as structural Verilog: 4 circuits, main circuit main
module main (
  input  [31:0] in_1,
  output [31:0] out_2
);

  wire buffer_1_out, buffer_2_out, buffer_3_out, buffer_4_out, buffer_5_out, clock_1_out, comparator_1_eq,
       not_1_out, not_2_out, register_5_q, register_10_q, timer_1_out_2;
  wire [31:0] _1, _2, _3, _4, _11, _21, _31, _41, a, b, c, d, multiplexer_1_out, multiplexer_2_out,
       multiplexer_3_out, multiplexer_4_out, multiplexer_5_out, multiplexer_6_out, multiplexer_7_out,
       multiplexer_8_out, multiplexer_9_out, multiplexer_10_out, multiplexer_11_out, multiplexer_12_out,
       multiplexer_14_out, register_1_q, register_2_q, register_3_q, register_4_q, register_6_q,
       register_7_q, register_8_q, register_9_q, timer_1_out_3;

  Multiplexer #(.width(32)) multiplexer_1 (.in0(a), .in1(32'h1), .out(multiplexer_1_out), .sel(in_1[0]));  // open: en
  Multiplexer #(.width(32)) multiplexer_2 (
    .in0(b), .in1({32{1'b0}}), .out(multiplexer_2_out), .sel(in_1[0]));  // open: en
  Multiplexer #(.width(32)) multiplexer_3 (
    .in0(c), .in1({32{1'b0}}), .out(multiplexer_3_out), .sel(in_1[0]));  // open: en
  Multiplexer #(.width(32)) multiplexer_4 (.in0(d), .in1(32'h1), .out(multiplexer_4_out), .sel(in_1[0]));  // open: en
  timer timer_1 (.in_1(in_1), .out_2(timer_1_out_2), .out_3(timer_1_out_3));
  // Probe on register_7_q
  doubleMULTI doublemulti_1 (
    .in_1(32'h1), .in_2({32{1'b0}}), .in_3({32{1'b0}}), .in_4(32'h1), .in_5(_1), .in_6(_2), .in_7(_3),
    .in_8(_4), .out_9(a), .out_10(b), .out_11(c), .out_12(d));
  Multiplexer #(.width(32)) multiplexer_5 (
    .in0(32'h1), .in1(_1), .out(multiplexer_5_out), .sel(register_5_q));  // open: en
  Multiplexer #(.width(32)) multiplexer_6 (
    .in0(32'h1), .in1(_2), .out(multiplexer_6_out), .sel(register_5_q));  // open: en
  Multiplexer #(.width(32)) multiplexer_7 (
    .in0(32'h1), .in1(_3), .out(multiplexer_7_out), .sel(register_5_q));  // open: en
  Multiplexer #(.width(32)) multiplexer_8 (
    .in0({32{1'b0}}), .in1(_4), .out(multiplexer_8_out), .sel(register_5_q));  // open: en
  Clock clock_1 (.out(clock_1_out));
  Multiplexer #(.width(32)) multiplexer_9 (
    .in0(multiplexer_1_out), .in1(_11), .out(multiplexer_9_out), .sel(buffer_1_out));  // open: en
  Multiplexer #(.width(32)) multiplexer_10 (
    .in0(multiplexer_2_out), .in1(_21), .out(multiplexer_10_out), .sel(buffer_1_out));  // open: en
  Multiplexer #(.width(32)) multiplexer_11 (
    .in0(multiplexer_3_out), .in1(_31), .out(multiplexer_11_out), .sel(buffer_1_out));  // open: en
  Multiplexer #(.width(32)) multiplexer_12 (
    .in0(multiplexer_4_out), .in1(_41), .out(multiplexer_12_out), .sel(buffer_1_out));  // open: en
  buf buffer_1 (buffer_1_out, buffer_3_out);
  buf buffer_2 (buffer_2_out, buffer_4_out);
  buf buffer_3 (buffer_3_out, buffer_2_out);
  buf buffer_4 (buffer_4_out, buffer_5_out);
  Comparator #(.width(32), .mode("unsigned")) comparator_1 (
    .a(timer_1_out_3), .b({32{1'b0}}), .eq(comparator_1_eq));  // open: gt, lt
  Register #(.width(32)) register_1 (.D(multiplexer_5_out), .Q(register_1_q), .clk(clock_1_out));  // open: en, clr
  Register #(.width(32)) register_2 (.D(multiplexer_6_out), .Q(register_2_q), .clk(clock_1_out));  // open: en, clr
  Register #(.width(32)) register_3 (.D(multiplexer_7_out), .Q(register_3_q), .clk(clock_1_out));  // open: en, clr
  Register #(.width(32)) register_4 (.D(multiplexer_8_out), .Q(register_4_q), .clk(clock_1_out));  // open: en, clr
  Register #(.width(1)) register_5 (.D(clock_1_out), .en(not_1_out), .Q(register_5_q), .clk(clock_1_out));  // open: clr
  not not_1 (not_1_out, register_5_q);
  Register #(.width(32)) register_6 (.D(multiplexer_9_out), .Q(register_6_q), .clk(timer_1_out_2));  // open: en, clr
  Register #(.width(32)) register_7 (.D(multiplexer_10_out), .Q(register_7_q), .clk(timer_1_out_2));  // open: en, clr
  Register #(.width(32)) register_8 (.D(multiplexer_11_out), .Q(register_8_q), .clk(timer_1_out_2));  // open: en, clr
  Register #(.width(32)) register_9 (.D(multiplexer_12_out), .Q(register_9_q), .clk(timer_1_out_2));  // open: en, clr
  buf buffer_5 (buffer_5_out, register_10_q);
  Register #(.width(1)) register_10 (
    .D(timer_1_out_2), .en(not_2_out), .Q(register_10_q), .clk(timer_1_out_2));  // open: clr
  not not_2 (not_2_out, register_10_q);
  Multiplexer #(.width(32)) multiplexer_13 (
    .in0({32{1'b0}}), .in1(multiplexer_14_out), .out(out_2), .sel(comparator_1_eq));  // open: en
  // Probe on register_1_q
  matrixMulti matrixmulti_1 (
    .in_1(register_1_q), .in_2(register_2_q), .in_3(register_3_q), .in_4(register_4_q), .out_5(_1),
    .out_6(_2), .out_7(_3), .out_8(_4));
  // Probe on register_6_q
  doubleMULTI doublemulti_2 (
    .in_1(register_6_q), .in_2(register_7_q), .in_3(register_8_q), .in_4(register_9_q), .in_5(_1), .in_6(_2),
    .in_7(_3), .in_8(_4), .out_9(_11), .out_10(_21), .out_11(_31), .out_12(_41));
  Multiplexer #(.width(32)) multiplexer_14 (
    .in0(register_7_q), .in1(register_6_q), .out(multiplexer_14_out), .sel(in_1[0]));  // open: en

  // Other names for the same wires on the sheet: yj = in_1[0]
endmodule

module matrixMulti (
  input  [31:0] in_1,
  input  [31:0] in_2,
  input  [31:0] in_3,
  input  [31:0] in_4,
  output [31:0] out_5,
  output [31:0] out_6,
  output [31:0] out_7,
  output [31:0] out_8
);

  wire [31:0] multiplier_1_out, multiplier_2_out, multiplier_3_out, multiplier_4_out, multiplier_5_out,
       multiplier_6_out, multiplier_7_out, multiplier_8_out;

  Multiplier #(.width(32)) multiplier_1 (.a(in_1), .b(in_1), .out(multiplier_1_out));  // open: cin, cout
  Multiplier #(.width(32)) multiplier_2 (.a(in_2), .b(in_3), .out(multiplier_2_out));  // open: cin, cout
  Multiplier #(.width(32)) multiplier_3 (.a(in_1), .b(in_2), .out(multiplier_3_out));  // open: cin, cout
  Multiplier #(.width(32)) multiplier_4 (.a(in_2), .b(in_4), .out(multiplier_4_out));  // open: cin, cout
  Multiplier #(.width(32)) multiplier_5 (.a(in_3), .b(in_1), .out(multiplier_5_out));  // open: cin, cout
  Multiplier #(.width(32)) multiplier_6 (.a(in_3), .b(in_4), .out(multiplier_6_out));  // open: cin, cout
  Multiplier #(.width(32)) multiplier_7 (.a(in_3), .b(in_2), .out(multiplier_7_out));  // open: cin, cout
  Multiplier #(.width(32)) multiplier_8 (.a(in_4), .b(in_4), .out(multiplier_8_out));  // open: cin, cout
  Adder #(.width(32)) adder_1 (.a(multiplier_1_out), .b(multiplier_2_out), .out(out_5));  // open: cin, cout
  Adder #(.width(32)) adder_2 (.a(multiplier_3_out), .b(multiplier_4_out), .out(out_6));  // open: cin, cout
  Adder #(.width(32)) adder_3 (.a(multiplier_5_out), .b(multiplier_6_out), .out(out_7));  // open: cin, cout
  Adder #(.width(32)) adder_4 (.a(multiplier_7_out), .b(multiplier_8_out), .out(out_8));  // open: cin, cout
endmodule

module doubleMULTI (
  input  [31:0] in_1,
  input  [31:0] in_2,
  input  [31:0] in_3,
  input  [31:0] in_4,
  input  [31:0] in_5,
  input  [31:0] in_6,
  input  [31:0] in_7,
  input  [31:0] in_8,
  output [31:0] out_9,
  output [31:0] out_10,
  output [31:0] out_11,
  output [31:0] out_12
);

  wire [31:0] multiplier_1_out, multiplier_2_out, multiplier_3_out, multiplier_4_out, multiplier_5_out,
       multiplier_6_out, multiplier_7_out, multiplier_8_out;

  Multiplier #(.width(32)) multiplier_1 (.a(in_1), .b(in_5), .out(multiplier_1_out));  // open: cin, cout
  Multiplier #(.width(32)) multiplier_2 (.a(in_2), .b(in_7), .out(multiplier_2_out));  // open: cin, cout
  Multiplier #(.width(32)) multiplier_3 (.a(in_1), .b(in_6), .out(multiplier_3_out));  // open: cin, cout
  Multiplier #(.width(32)) multiplier_4 (.a(in_2), .b(in_8), .out(multiplier_4_out));  // open: cin, cout
  Multiplier #(.width(32)) multiplier_5 (.a(in_3), .b(in_5), .out(multiplier_5_out));  // open: cin, cout
  Multiplier #(.width(32)) multiplier_6 (.a(in_4), .b(in_7), .out(multiplier_6_out));  // open: cin, cout
  Multiplier #(.width(32)) multiplier_7 (.a(in_3), .b(in_5), .out(multiplier_7_out));  // open: cin, cout
  Multiplier #(.width(32)) multiplier_8 (.a(in_4), .b(in_7), .out(multiplier_8_out));  // open: cin, cout
  Adder #(.width(32)) adder_1 (.a(multiplier_1_out), .b(multiplier_2_out), .out(out_9));  // open: cin, cout
  Adder #(.width(32)) adder_2 (.a(multiplier_3_out), .b(multiplier_4_out), .out(out_10));  // open: cin, cout
  Adder #(.width(32)) adder_3 (.a(multiplier_5_out), .b(multiplier_6_out), .out(out_11));  // open: cin, cout
  Adder #(.width(32)) adder_4 (.a(multiplier_7_out), .b(multiplier_8_out), .out(out_12));  // open: cin, cout

  // Other names for the same wires on the sheet: _81[31:0] = in_1; _82[31:0] = in_2; _83[31:0] = in_3;
  //   _84[31:0] = in_4; _85[31:0] = in_5; _86[31:0] = in_6; _87[31:0] = in_7; _88[31:0] = in_8
endmodule

module timer (
  input  [31:0] in_1,
  output out_2,
  output [31:0] out_3
);

  wire buffer_1_out, buffer_2_out, buffer_3_out, buffer_4_out, buffer_5_out, buffer_6_out, buffer_7_out,
       buffer_8_out, buffer_9_out, buffer_10_out, clock_1_out, not_1_out, register_2_q;
  wire [31:0] divider_1_out, divider_1_rem, multiplexer_1_out, register_3_q;

  Multiplexer #(.width(32)) multiplexer_1 (
    .in0(in_1), .in1(out_3), .out(multiplexer_1_out), .sel(register_2_q));  // open: en
  Clock clock_1 (.out(clock_1_out));
  // Probe on multiplexer_1_out
  buf buffer_1 (buffer_1_out, buffer_2_out);
  // Probe on nothing
  Register #(.width(32)) register_1 (.D(divider_1_out), .Q(out_3), .clk(clock_1_out));  // open: en, clr
  Divider #(.width(32)) divider_1 (
    .a(multiplexer_1_out), .b(32'h2), .out(divider_1_out), .rem(divider_1_rem));  // open: upper
  Register #(.width(1)) register_2 (.D(clock_1_out), .en(not_1_out), .Q(register_2_q), .clk(clock_1_out));  // open: clr
  not not_1 (not_1_out, register_2_q);
  // Probe on divider_1_rem
  and and_1 (out_2, buffer_1_out, register_3_q[0]);
  buf buffer_2 (buffer_2_out, buffer_3_out);
  buf buffer_3 (buffer_3_out, buffer_4_out);
  buf buffer_4 (buffer_4_out, buffer_5_out);
  buf buffer_5 (buffer_5_out, buffer_6_out);
  buf buffer_6 (buffer_6_out, buffer_7_out);
  buf buffer_7 (buffer_7_out, buffer_8_out);
  buf buffer_8 (buffer_8_out, buffer_9_out);
  buf buffer_9 (buffer_9_out, buffer_10_out);
  buf buffer_10 (buffer_10_out, clock_1_out);
  Register #(.width(32)) register_3 (.D(divider_1_rem), .Q(register_3_q), .clk(clock_1_out));  // open: en, clr
endmodule
