// Logisim project fib[x].circ as structural Verilog: 1 circuit, main circuit main
module main (
  input  [2:0] in_1,
  output [3:0] out_2
);

  wire clock_1_out, clock_2_out, clock_3_out, comparator_1_eq, comparator_1_gt, comparator_2_eq, not_1_out,
       not_2_out, not_3_out, not_4_out, not_5_out, not_6_out, or_1_out, register_1_q, register_7_q;
  wire [2:0] adder_1_out, adder_3_out, register_5_q;
  wire [3:0] _1, adder_2_out, multiplexer_1_out, register_2_q, register_3_q, register_6_q;

  Clock clock_1 (.out(clock_1_out));
  Multiplexer #(.width(4)) multiplexer_1 (
    .in0(4'b0001), .in1(_1), .out(multiplexer_1_out), .sel(register_1_q));  // open: en
  not not_1 (not_1_out, clock_2_out);
  Register #(.width(1)) register_1 (.D(not_1_out), .en(not_2_out), .Q(register_1_q), .clk(clock_1_out));  // open: clr
  not not_2 (not_2_out, register_1_q);
  Register #(.width(4)) register_2 (.D(register_3_q), .Q(register_2_q), .clk(clock_2_out));  // open: en, clr
  Register #(.width(4)) register_3 (.D(multiplexer_1_out), .Q(register_3_q), .clk(clock_2_out));  // open: en, clr
  Register #(.width(4)) register_4 (.D(adder_2_out), .en(not_5_out), .Q(_1), .clk(not_3_out));  // open: clr
  Clock clock_2 (.out(clock_2_out));
  not not_3 (not_3_out, clock_2_out);
  Register #(.width(3)) register_5 (.D(adder_3_out), .Q(register_5_q), .clk(not_4_out));  // open: en, clr
  not not_4 (not_4_out, clock_2_out);
  // Probe on adder_1_out
  Comparator #(.width(3), .mode("unsigned")) comparator_1 (
    .a(adder_1_out), .b(in_1), .gt(comparator_1_gt), .eq(comparator_1_eq));  // open: lt
  Comparator #(.width(3), .mode("unsigned")) comparator_2 (.a(in_1), .b(3'b001), .eq(comparator_2_eq));  // open: gt, lt
  not not_5 (not_5_out, register_7_q);
  Adder #(.width(3)) adder_1 (.a(register_5_q), .b(3'b001), .out(adder_1_out));  // open: cin, cout
  or or_1 (or_1_out, comparator_1_gt, comparator_1_eq);
  Adder #(.width(4)) adder_2 (.a(register_2_q), .b(register_3_q), .out(adder_2_out));  // open: cin, cout
  Adder #(.width(3)) adder_3 (.a(register_5_q), .b(3'b001), .out(adder_3_out));  // open: cin, cout
  Multiplexer #(.width(4)) multiplexer_2 (
    .in0(register_6_q), .in1(4'b0001), .out(out_2), .sel(comparator_2_eq));  // open: en
  Register #(.width(4)) register_6 (.D(_1), .Q(register_6_q), .clk(clock_2_out), .clr(not_5_out));  // open: en
  Register #(.width(1)) register_7 (.D(or_1_out), .en(not_6_out), .Q(register_7_q), .clk(clock_3_out));  // open: clr
  Clock clock_3 (.out(clock_3_out));
  not not_6 (not_6_out, register_7_q);
endmodule
