// Logisim project mod5.circ as structural Verilog: 2 circuits, main circuit mod5
module mod5 (
  input  in_1,
  output out_2,
  output out_3,
  output out_4,
  output out_5,
  output out_6
);

  wire clock_1_out, undriven;
  wire [4:0] register_1_q;

  Register #(.width(5)) register_1 (
    .D({out_6, out_5, out_4, out_3, out_2}), .Q(register_1_q), .clk(clock_1_out), .clr(undriven));  // open: en
  Clock clock_1 (.out(clock_1_out));
  fuc fuc_1 (
    .in(in_1), .s0(register_1_q[0]), .s1(register_1_q[1]), .s2(register_1_q[2]), .s3(register_1_q[3]),
    .s4(register_1_q[4]), .s0_2(out_2), .s1_2(out_3), .s2_2(out_4), .s3_2(out_5), .s4_2(out_6));
endmodule

module fuc (
  input  in,
  input  s0,
  input  s1,
  input  s2,
  input  s3,
  input  s4,
  output s0_2,
  output s1_2,
  output s2_2,
  output s3_2,
  output s4_2
);

  wire and_1_out, and_2_out, and_3_out, and_4_out, and_5_out, and_6_out, and_7_out, and_8_out, not_1_out,
       not_2_out, not_3_out, not_4_out, not_5_out, not_6_out, not_7_out, not_8_out, not_9_out;

  not not_1 (not_1_out, in);
  not not_2 (not_2_out, s0);
  not not_3 (not_3_out, s2);
  not not_4 (not_4_out, s3);
  not not_5 (not_5_out, s0);
  not not_6 (not_6_out, s2);
  not not_7 (not_7_out, s3);
  and and_1 (and_1_out, in, s3);
  and and_2 (and_2_out, in, s2);
  not not_8 (not_8_out, in);
  not not_9 (not_9_out, in);
  and and_3 (and_3_out, not_1_out, not_2_out);
  and and_4 (and_4_out, not_3_out, not_4_out);
  and and_5 (and_5_out, in, not_5_out);
  and and_6 (and_6_out, not_6_out, not_7_out);
  or or_1 (s3_2, and_1_out, and_2_out);
  and and_7 (and_7_out, not_8_out, s3);
  and and_8 (and_8_out, not_9_out, s2);
  and and_9 (s1_2, and_3_out, and_4_out);
  and and_10 (s2_2, and_5_out, and_6_out);
  or or_2 (s4_2, and_7_out, and_8_out);

  assign s0_2 = s0;
endmodule
