// Logisim project 4bitALU.circ as structural Verilog: 1 circuit, main circuit alu
module alu (
  input  [3:0] A,
  input  [3:0] B,
  input  [1:0] ALUOp,
  output [3:0] out_4
);

  wire [3:0] _1, _2, _3, _4;

  Adder #(.width(4)) adder_1 (.a(A), .b(B), .out(_1));  // open: cin, cout
  Subtractor #(.width(4)) subtractor_1 (.a(A), .b(B), .out(_2));  // open: bin, bout
  and and_1 (_3[3], B[3], A[3]);
  and and_2 (_3[2], B[2], A[2]);
  and and_3 (_3[1], B[1], A[1]);
  and and_4 (_3[0], B[0], A[0]);
  or or_1 (_4[3], B[3], A[3]);
  or or_2 (_4[2], B[2], A[2]);
  or or_3 (_4[1], B[1], A[1]);
  or or_4 (_4[0], B[0], A[0]);
  Multiplexer #(.select(2), .width(4)) multiplexer_1 (
    .in0(_1), .in1(_2), .in2(_3), .in3(_4), .out(out_4), .sel(ALUOp));  // open: en
endmodule
