// Logisim project CRC.circ as structural Verilog: 2 circuits, main circuit 4mod2
module _4mod2 (
  input  [3:0] in_1,
  input  [3:0] in_2,
  output [2:0] out_3,
  output out_4
);

  wire [3:0] multiplier_1_out;
  wire [3:1] divider_1_out;

  Divider #(.width(4)) divider_1 (.a(in_1), .b(in_2), .out({divider_1_out, out_4}));  // open: upper, rem
  Multiplier #(.width(4)) multiplier_1 (.a({3'b000, in_1[3]}), .b(in_2), .out(multiplier_1_out));  // open: cin, cout
  // XOR_Gate xor_1 has open pins: in0=multiplier_1_out[3], in4=in_1[3], out=open
  xor xor_2 (out_3[2], multiplier_1_out[2], in_1[2]);
  xor xor_3 (out_3[1], multiplier_1_out[1], in_1[1]);
  xor xor_4 (out_3[0], multiplier_1_out[0], in_1[0]);
endmodule

module CRC (
  input  [7:0] A,
  input  [3:0] B,
  output [10:0] out_3
);

  wire [2:0] _2, _3, _4, _5, _6, _7, _8;

  _4mod2 u_4mod2_1 (.in_1(A[7:4]), .in_2(B), .out_3(_8));  // open: out_4
  _4mod2 u_4mod2_2 (.in_1({_8, A[3]}), .in_2(B), .out_3(_7));  // open: out_4
  _4mod2 u_4mod2_3 (.in_1({_7, A[2]}), .in_2(B), .out_3(_6));  // open: out_4
  _4mod2 u_4mod2_4 (.in_1({_6, A[1]}), .in_2(B), .out_3(_5));  // open: out_4
  _4mod2 u_4mod2_5 (.in_1({_5, A[0]}), .in_2(B), .out_3(_4));  // open: out_4
  _4mod2 u_4mod2_6 (.in_1({_4, 1'b0}), .in_2(B), .out_3(_3));  // open: out_4
  _4mod2 u_4mod2_7 (.in_1({_3, 1'b0}), .in_2(B), .out_3(_2));  // open: out_4
  _4mod2 u_4mod2_8 (.in_1({_2, 1'b0}), .in_2(B), .out_3(out_3[2:0]));  // open: out_4

  assign out_3[10:3] = A;

  // Other names for the same wires on the sheet: _1[2:0] = out_3[2:0]; b_t = A[0]; a_t = A[1]
endmodule
