// Logisim project fsm-p0.circ as structural Verilog: 3 circuits, main circuit fsm
module fsm (
  input  CLR,
  input  [1:0] In,
  output out_3
);

  wire clock_1_out;
  wire [2:0] func_1_ss2, multiplexer_1_out, register_1_q;

  Clock clock_1 (.out(clock_1_out));
  func func_1 (
    .state0(register_1_q[2]), .s1(register_1_q[1]), .s2(register_1_q[0]), .In0(In[1]), .In1(In[0]),
    .ss0(func_1_ss2[2]), .ss1(func_1_ss2[1]), .ss2(func_1_ss2[0]));
  Multiplexer #(.width(3)) multiplexer_1 (
    .in0(func_1_ss2), .in1(3'b000), .out(multiplexer_1_out), .sel(CLR));  // open: en
  Register #(.width(3)) register_1 (.D(multiplexer_1_out), .Q(register_1_q), .clk(clock_1_out));  // open: en, clr
  outlook outlook_1 (
    .s0(register_1_q[2]), .s1(register_1_q[1]), .s2(register_1_q[0]), .i0(In[1]), .i1(In[0]), .out(out_3));
endmodule

module func (
  input  state0,
  input  s1,
  input  s2,
  input  In0,
  input  In1,
  output ss0,
  output ss1,
  output ss2
);

  wire and_1_out, and_3_out, and_4_out, and_5_out, and_6_out, and_7_out, and_8_out, and_9_out, and_10_out,
       and_11_out, and_12_out, and_13_out, and_14_out, and_15_out, and_16_out, and_17_out, and_18_out,
       and_19_out, and_20_out, not_1_out, not_2_out, not_3_out, not_4_out, not_5_out, not_6_out, not_7_out,
       not_8_out, not_9_out, not_10_out, not_11_out, not_12_out, not_13_out, not_14_out, not_15_out,
       not_16_out, not_17_out, or_1_out, or_2_out, or_3_out, or_4_out;

  and and_1 (and_1_out, s1, s2);
  not not_1 (not_1_out, In1);
  not not_2 (not_2_out, s1);
  not not_3 (not_3_out, s1);
  not not_4 (not_4_out, s2);
  not not_5 (not_5_out, s2);
  not not_6 (not_6_out, s1);
  not not_7 (not_7_out, s2);
  not not_8 (not_8_out, In0);
  not not_9 (not_9_out, s1);
  not not_10 (not_10_out, s2);
  not not_11 (not_11_out, In0);
  and and_2 (ss0, and_1_out, not_1_out);
  and and_3 (and_3_out, not_2_out, s2);
  not not_12 (not_12_out, In0);
  and and_4 (and_4_out, not_3_out, s2);
  not not_13 (not_13_out, In1);
  and and_5 (and_5_out, s1, not_4_out);
  not not_14 (not_14_out, In0);
  and and_6 (and_6_out, s1, not_5_out);
  not not_15 (not_15_out, In1);
  and and_7 (and_7_out, not_6_out, not_7_out);
  and and_8 (and_8_out, not_8_out, In1);
  and and_9 (and_9_out, not_9_out, s2);
  not not_16 (not_16_out, In1);
  and and_10 (and_10_out, s1, not_10_out);
  not not_17 (not_17_out, In1);
  and and_11 (and_11_out, s1, s2);
  and and_12 (and_12_out, not_11_out, In1);
  and and_13 (and_13_out, and_3_out, not_12_out);
  or or_1 (or_1_out, and_13_out, and_14_out);
  and and_14 (and_14_out, and_4_out, not_13_out);
  and and_15 (and_15_out, and_5_out, not_14_out);
  or or_2 (or_2_out, and_15_out, and_16_out);
  and and_16 (and_16_out, and_6_out, not_15_out);
  and and_17 (and_17_out, and_7_out, and_8_out);
  or or_3 (or_3_out, and_17_out, and_18_out);
  and and_18 (and_18_out, and_9_out, not_16_out);
  and and_19 (and_19_out, and_10_out, not_17_out);
  or or_4 (or_4_out, and_19_out, and_20_out);
  and and_20 (and_20_out, and_11_out, and_12_out);
  or or_5 (ss1, or_1_out, or_2_out);
  or or_6 (ss2, or_3_out, or_4_out);
endmodule

module outlook (
  input  s0,
  input  s1,
  input  s2,
  input  i0,
  input  i1,
  output out
);

  wire and_1_out, and_2_out, not_1_out, not_2_out;

  not not_1 (not_1_out, s0);
  not not_2 (not_2_out, i1);
  and and_1 (and_1_out, not_1_out, s1);
  and and_2 (and_2_out, s2, not_2_out);
  and and_3 (out, and_1_out, and_2_out);
endmodule
