// Logisim project swap.circ as structural Verilog
module swap (
  input  I1,
  input  I2,
  input  S,
  output O1,
  output O2
);

  wire and_1_out, and_2_out, or_1_out, or_2_out, xor_1_out, xor_2_out;

  xor xor_1 (xor_1_out, S, or_1_out);
  and and_1 (and_1_out, I1, S);
  or or_1 (or_1_out, S, I1);
  or or_2 (or_2_out, S, I2);
  and and_2 (and_2_out, S, I2);
  xor xor_2 (xor_2_out, or_2_out, S);
  or or_3 (O1, xor_1_out, and_2_out);
  or or_4 (O2, and_1_out, xor_2_out);
endmodule
