// Logisim project cpu_logisim (2).circ as structural Verilog: 8 circuits, main circuit main
module main (
  input  in_1,
  output [31:0] out_2,
  output out_3,
  output [4:0] out_4,
  output [31:0] out_5,
  output out_6,
  output [4:0] out_7,
  output [31:0] out_8
);

  wire alu_1_zero, and_1_out, clk, controller_1_alusrc, controller_1_branch, controller_1_memread,
       controller_1_memtoreg, controller_1_regdst, LUI;
  wire [1:0] ALUOp;
  wire [3:0] extender_1_aluout;
  wire [27:0] shifter_1_out;
  wire [31:0] adder_1_out, adder_2_out, alu_1_out, extender_1_out, grf_1_rd1, ifu_1_pc, multiplexer_2_out,
       multiplexer_3_out, multiplexer_4_out, shifter_2_out;

  Clock clock_1 (.out(clk));
  IFU ifu_1 (.NEWpc(multiplexer_4_out), .clk(clk), .reset(in_1), .pc(ifu_1_pc), .out(out_2));
  Adder #(.width(32)) adder_1 (.a(ifu_1_pc), .b(32'h4), .out(adder_1_out));  // open: cin, cout
  // Probe on adder_1_out
  controller controller_1 (
    .in_1(out_2[31:26]), .RegDst(controller_1_regdst), .ALUSrc(controller_1_alusrc),
    .MemtoReg(controller_1_memtoreg), .RegWrite(out_3), .MemRead(controller_1_memread), .MemWrite(out_6),
    .Branch(controller_1_branch), .ALUOp1(ALUOp[1]), .ALUOp2(ALUOp[0]), .LUI(LUI));
  Shifter #(.width(28)) shifter_1 (.in(out_2[27:0]), .\dist (5'b00010), .out(shifter_1_out));
  Multiplexer #(.width(5)) multiplexer_1 (
    .in0(out_2[20:16]), .in1(out_2[15:11]), .out(out_4), .sel(controller_1_regdst));  // open: en
  // Probe on nothing
  grf grf_1 (
    .reset(in_1), .WE(out_3), .A1(out_2[25:21]), .A2(out_2[20:16]), .A3(out_4), .WD(out_5), .in_7(clk),
    .RD1(grf_1_rd1), .RD2(out_8));
  extender extender_1 (
    .func(out_2[5:0]), .dataIn(out_2), .ori(ALUOp[0]), .lui(LUI), .ALUOp(ALUOp), .out(extender_1_out),
    .ALUout(extender_1_aluout));
  Shifter #(.width(32)) shifter_2 (.in(extender_1_out), .\dist (5'b00010), .out(shifter_2_out));
  Multiplexer #(.width(32)) multiplexer_2 (
    .in0(out_8), .in1(extender_1_out), .out(multiplexer_2_out), .sel(controller_1_alusrc));  // open: en
  Adder #(.width(32)) adder_2 (.a(adder_1_out), .b(shifter_2_out), .out(adder_2_out));  // open: cin, cout
  ALU alu_1 (
    .in1(grf_1_rd1), .in2(multiplexer_2_out), .ALUcontrol(extender_1_aluout), .zero(alu_1_zero),
    .out(alu_1_out));
  Multiplexer #(.width(32)) multiplexer_3 (
    .in0(adder_1_out), .in1(adder_2_out), .out(multiplexer_3_out), .sel(and_1_out));  // open: en
  and and_1 (and_1_out, alu_1_zero, controller_1_branch);
  Multiplexer #(.width(32)) multiplexer_4 (
    .in0(multiplexer_3_out), .in1({adder_1_out[31:28], shifter_1_out}), .out(multiplexer_4_out), .sel(1'b0));  // open: en
  DM dm_1 (
    .write(out_6), .read(controller_1_memread), .select(controller_1_memtoreg), .add(alu_1_out),
    .reset(in_1), .clk(clk), .data(out_8), .out(out_5), .Memadd(out_7));

  // Other names for the same wires on the sheet: ori = ALUOp[0]; instr[31:0] = out_2; MemAddr[4:0] = out_7;
  //   MemData[31:0] = out_8; MemWrite = out_6; RegAddr[4:0] = out_4; RegData[31:0] = out_5; RegWrite = out_3;
  //   reset = in_1
endmodule

module grf (
  input  reset,
  input  WE,
  input  [4:0] A1,
  input  [4:0] A2,
  input  [4:0] A3,
  input  [31:0] WD,
  input  in_7,
  output [31:0] RD1,
  output [31:0] RD2
);

  wire [31:0] i0, i1, i2, i3, i4, i5, i6, i7, i8, i9, i10, i11, i12, i13, i14, i15, i16, i17, i18, i19, i20,
       i21, i22, i23, i24, i25, i26, i27, i28, i29, i30, i31, o0, o1, o2, o3, o4, o5, o6, o7, o8, o9, o10,
       o11, o12, o13, o14, o15, o16, o17, o18, o19, o20, o21, o22, o23, o24, o25, o26, o27, o28, o29, o30,
       o31, undriven;

  Multiplexer #(.select(5), .width(32), .disabled(0)) multiplexer_1 (
    .in0(o0), .in1(o1), .in2(o2), .in3(o3), .in4(o4), .in5(o5), .in6(o6), .in7(o7), .in8(o8), .in9(o9),
    .in10(o10), .in11(o11), .in12(o12), .in13(o13), .in14(o14), .in15(o15), .in16(o16), .in17(o17),
    .in18(o18), .in19(o19), .in20(o20), .in21(o21), .in22(o22), .in23(o23), .in24(o24), .in25(o25),
    .in26(o26), .in27(o27), .in28(o28), .in29(o29), .in30(o30), .in31(o31), .out(RD1), .sel(A1));  // open: en
  Multiplexer #(.select(5), .width(32), .disabled(0)) multiplexer_2 (
    .in0(o0), .in1(o1), .in2(o2), .in3(o3), .in4(o4), .in5(o5), .in6(o6), .in7(o7), .in8(o8), .in9(o9),
    .in10(o10), .in11(o11), .in12(o12), .in13(o13), .in14(o14), .in15(o15), .in16(o16), .in17(o17),
    .in18(o18), .in19(o19), .in20(o20), .in21(o21), .in22(o22), .in23(o23), .in24(o24), .in25(o25),
    .in26(o26), .in27(o27), .in28(o28), .in29(o29), .in30(o30), .in31(o31), .out(RD2), .sel(A2));  // open: en
  Register #(.width(32)) register_1 (.D(undriven), .en(WE), .Q(o0), .clk(in_7), .clr(1'b1));
  Register #(.width(32)) register_2 (.D(i4), .en(WE), .Q(o4), .clk(in_7), .clr(reset));
  Register #(.width(32)) register_3 (.D(i8), .en(WE), .Q(o8), .clk(in_7), .clr(reset));
  Register #(.width(32)) register_4 (.D(i12), .en(WE), .Q(o12), .clk(in_7), .clr(reset));
  Register #(.width(32)) register_5 (.D(i16), .en(WE), .Q(o16), .clk(in_7), .clr(reset));
  Register #(.width(32)) register_6 (.D(i20), .en(WE), .Q(o20), .clk(in_7), .clr(reset));
  Register #(.width(32)) register_7 (.D(i24), .en(WE), .Q(o24), .clk(in_7), .clr(reset));
  Register #(.width(32)) register_8 (.D(i28), .en(WE), .Q(o28), .clk(in_7), .clr(reset));
  Register #(.width(32)) register_9 (.D(i1), .en(WE), .Q(o1), .clk(in_7), .clr(reset));
  Register #(.width(32)) register_10 (.D(i5), .en(WE), .Q(o5), .clk(in_7), .clr(reset));
  Register #(.width(32)) register_11 (.D(i9), .en(WE), .Q(o9), .clk(in_7), .clr(reset));
  Register #(.width(32)) register_12 (.D(i13), .en(WE), .Q(o13), .clk(in_7), .clr(reset));
  Register #(.width(32)) register_13 (.D(i17), .en(WE), .Q(o17), .clk(in_7), .clr(reset));
  Register #(.width(32)) register_14 (.D(i21), .en(WE), .Q(o21), .clk(in_7), .clr(reset));
  Register #(.width(32)) register_15 (.D(i25), .en(WE), .Q(o25), .clk(in_7), .clr(reset));
  Register #(.width(32)) register_16 (.D(i29), .en(WE), .Q(o29), .clk(in_7), .clr(reset));
  Demultiplexer #(.select(5), .width(32), .tristate("true"), .disabled(0)) demultiplexer_1 (
    .out0(i0), .out1(i1), .out2(i2), .out3(i3), .out4(i4), .out5(i5), .out6(i6), .out7(i7), .out8(i8),
    .out9(i9), .out10(i10), .out11(i11), .out12(i12), .out13(i13), .out14(i14), .out15(i15), .out16(i16),
    .out17(i17), .out18(i18), .out19(i19), .out20(i20), .out21(i21), .out22(i22), .out23(i23), .out24(i24),
    .out25(i25), .out26(i26), .out27(i27), .out28(i28), .out29(i29), .out30(i30), .out31(i31), .in(WD),
    .sel(A3));  // open: en
  Register #(.width(32)) register_17 (.D(i2), .en(WE), .Q(o2), .clk(in_7), .clr(reset));
  Register #(.width(32)) register_18 (.D(i6), .en(WE), .Q(o6), .clk(in_7), .clr(reset));
  Register #(.width(32)) register_19 (.D(i10), .en(WE), .Q(o10), .clk(in_7), .clr(reset));
  Register #(.width(32)) register_20 (.D(i14), .en(WE), .Q(o14), .clk(in_7), .clr(reset));
  Register #(.width(32)) register_21 (.D(i18), .en(WE), .Q(o18), .clk(in_7), .clr(reset));
  Register #(.width(32)) register_22 (.D(i22), .en(WE), .Q(o22), .clk(in_7), .clr(reset));
  Register #(.width(32)) register_23 (.D(i26), .en(WE), .Q(o26), .clk(in_7), .clr(reset));
  Register #(.width(32)) register_24 (.D(i30), .en(WE), .Q(o30), .clk(in_7), .clr(reset));
  Register #(.width(32)) register_25 (.D(i3), .en(WE), .Q(o3), .clk(in_7), .clr(reset));
  Register #(.width(32)) register_26 (.D(i7), .en(WE), .Q(o7), .clk(in_7), .clr(reset));
  Register #(.width(32)) register_27 (.D(i11), .en(WE), .Q(o11), .clk(in_7), .clr(reset));
  Register #(.width(32)) register_28 (.D(i15), .en(WE), .Q(o15), .clk(in_7), .clr(reset));
  Register #(.width(32)) register_29 (.D(i19), .en(WE), .Q(o19), .clk(in_7), .clr(reset));
  Register #(.width(32)) register_30 (.D(i23), .en(WE), .Q(o23), .clk(in_7), .clr(reset));
  Register #(.width(32)) register_31 (.D(i27), .en(WE), .Q(o27), .clk(in_7), .clr(reset));
  Register #(.width(32)) register_32 (.D(i31), .en(WE), .Q(o31), .clk(in_7), .clr(reset));

  // Other names for the same wires on the sheet: clear = reset; clk = in_7; en = WE
endmodule

module ALU (
  input  [31:0] in1,
  input  [31:0] in2,
  input  [3:0] ALUcontrol,
  output zero,
  output [31:0] out
);

  wire [31:0] adder_1_out, and_1_out, or_1_out, subtractor_1_out;

  assign and_1_out = in1 & in2;  // AND_Gate and_1, 32 bits wide
  Adder #(.width(32)) adder_1 (.a(in1), .b(in2), .out(adder_1_out));  // open: cin, cout
  Subtractor #(.width(32)) subtractor_1 (.a(in1), .b(in2), .out(subtractor_1_out));  // open: bin, bout
  assign or_1_out = in1 | in2;  // OR_Gate or_1, 32 bits wide
  Comparator #(.width(32)) comparator_1 (.a(in1), .b(in2), .eq(zero));  // open: gt, lt
  Multiplexer #(.select(4), .width(32)) multiplexer_1 (
    .in0(and_1_out), .in1(or_1_out), .in2(adder_1_out), .in6(subtractor_1_out), .out(out), .sel(ALUcontrol));  // open: in3, in4, in5, in7, in8, in9, in10, in11, in12, in13, in14, in15, en
endmodule

module alucon (
  input  [1:0] in_1,
  input  [5:0] in_2,
  output [3:0] out_3
);

  wire and_1_out, not_1_out;
  wire [1:1] not_2_out, not_3_out;

  not not_1 (not_1_out, in_1[0]);
  not not_2 (not_2_out[1], in_1[0]);
  and and_1 (and_1_out, in_1[1], not_1_out);
  not not_3 (not_3_out[1], 1'b0);
  Multiplexer #(.width(4)) multiplexer_1 (
    .in0({2'b00, not_2_out[1], in_1[0]}), .in1({1'b0, in_2[1], not_3_out[1], 1'b0}), .out(out_3),
    .sel(and_1_out));  // open: en
endmodule

module controller (
  input  [5:0] in_1,
  output RegDst,
  output ALUSrc,
  output MemtoReg,
  output RegWrite,
  output MemRead,
  output MemWrite,
  output Branch,
  output ALUOp1,
  output ALUOp2,
  output LUI
);

  wire beq_out, lw_out, not_1_out, not_2_out, not_3_out, not_4_out, not_5_out, not_6_out, ori_out, R_mat_out,
       sw_out;

  not not_1 (not_1_out, in_1[5]);
  not not_2 (not_2_out, in_1[4]);
  not not_3 (not_3_out, in_1[3]);
  not not_4 (not_4_out, in_1[2]);
  not not_5 (not_5_out, in_1[0]);
  not not_6 (not_6_out, in_1[1]);
  and R_mat (R_mat_out, not_5_out, not_6_out, not_4_out, not_3_out, not_2_out, not_1_out);
  and ori (ori_out, not_1_out, not_2_out, in_1[3], in_1[2], not_6_out, in_1[0]);
  and lw (lw_out, in_1[5], not_2_out, not_3_out, not_4_out, in_1[1], in_1[0]);
  and sw (sw_out, in_1[5], not_2_out, in_1[3], not_4_out, in_1[1], in_1[0]);
  and beq (beq_out, not_1_out, not_2_out, not_3_out, in_1[2], not_6_out, not_5_out);
  and u_lui (LUI, not_1_out, not_2_out, in_1[3], in_1[2], in_1[1], in_1[0]);
  buf or_1 (RegDst, R_mat_out);  // OR_Gate
  or or_2 (ALUSrc, ori_out, lw_out, sw_out, LUI);
  buf or_3 (MemtoReg, lw_out);  // OR_Gate
  or or_4 (RegWrite, R_mat_out, ori_out, lw_out, LUI);
  buf or_5 (MemRead, lw_out);  // OR_Gate
  buf or_6 (MemWrite, sw_out);  // OR_Gate
  buf or_7 (Branch, beq_out);  // OR_Gate
  buf or_8 (ALUOp1, R_mat_out);  // OR_Gate
  buf or_9 (ALUOp2, ori_out);  // OR_Gate
endmodule

module IFU (
  input  [31:0] NEWpc,
  input  clk,
  input  reset,
  output [31:0] pc,
  output [31:0] out
);

  wire [31:0] divider_1_out;

  Register #(.width(32)) u_PC (.D(NEWpc), .Q(pc), .clk(clk), .clr(reset));  // open: en
  Divider #(.width(32)) divider_1 (.a(pc), .b(32'h4), .out(divider_1_out));  // open: upper, rem
  ROM #(.addrWidth(5), .dataWidth(32)) rom_1 (.addr(divider_1_out[4:0]), .data(out));  // open: sel

  // Notes on the sheet:
  //   contents of rom_1 (hex, n*v repeats v):
  //   36100003 ac100004 1200fffd 2108821 2309023 8c100003 1200fff9
endmodule

module DM (
  input  write,
  input  read,
  input  select,
  input  [31:0] add,
  input  reset,
  input  clk,
  input  [31:0] data,
  output [31:0] out,
  output [4:0] Memadd
);

  wire [31:0] ram_1_data;
  wire [31:5] divider_1_out;

  Divider #(.width(32)) divider_1 (.a(add), .b(32'h4), .out({divider_1_out, Memadd}));  // open: upper, rem
  RAM #(.addrWidth(5), .dataWidth(32), .bus("separate")) ram_1 (
    .addr(Memadd), .din(data), .data(ram_1_data), .str(write), .clk(clk), .ld(read), .clr(reset));  // open: sel
  Multiplexer #(.width(32)) multiplexer_1 (.in0(add), .in1(ram_1_data), .out(out), .sel(select));  // open: en
endmodule

module extender (
  input  [5:0] func,
  input  [31:0] dataIn,
  input  ori,
  input  lui,
  input  [1:0] ALUOp,
  output [31:0] out,
  output [3:0] ALUout
);

  wire not_1_out;
  wire [31:0] bit_extender_1_out, bit_extender_2_out, multiplexer_1_out;

  assign bit_extender_1_out = {{16{1'b0}}, dataIn[15:0]};  // Bit_Extender bit_extender_1
  assign bit_extender_2_out = {{16{dataIn[15]}}, dataIn[15:0]};  // Bit_Extender bit_extender_2
  Multiplexer #(.width(32)) multiplexer_1 (
    .in0(bit_extender_1_out), .in1(bit_extender_2_out), .out(multiplexer_1_out), .sel(not_1_out));  // open: en
  not not_1 (not_1_out, ori);
  Multiplexer #(.width(32)) multiplexer_2 (
    .in0(multiplexer_1_out), .in1({dataIn[15:0], {16{1'b0}}}), .out(out), .sel(lui));  // open: en
  alucon alucon_1 (.in_1(ALUOp), .in_2(func), .out_3(ALUout));
endmodule
